// Logisim project CPU.circ as structural Verilog: 6 circuits, main circuit main
module main (
  input  in_1,
  input  \中断信号 ,
  input  [15:0] in_3
);

  wire and_2_out, and_3_out, and_4_out, and_5_out, and_6_out, and_7_out, and_8_out, CLK, clock_1_out,
       clock_2_out, clock_3_out, clock_4_out, d_ff_1_q, d_ff_2_q, d_ff_3_qn, iftoex_1_out_22,
       iftoex_1_out_24, iftoex_1_out_27, iftoex_1_out_29, iftoex_1_out_31, iftoex_1_out_33, iftoex_1_out_34,
       iftoex_1_out_35, iftoex_1_out_36, j_k_ff_1_q, j_k_ff_1_qn, j_k_ff_2_q, multiplexer_15_out, nor_1_out,
       nor_2_out, nor_3_out, nor_4_out, not_1_out, not_2_out, not_3_out, not_4_out, or_1_out, or_2_out,
       or_3_out, or_4_out;
  wire [1:0] iftoex_1_out_21, iftoex_1_out_26, iftoex_1_output_bus_4, multiplexer_9_out, register0_1_out_12,
       xor_1_out, xor_2_out, xor_3_out, xor_4_out;
  wire [2:0] alu_1_output_bus_1, demultiplexer_1_out0, demultiplexer_1_out1, iftoex_1_out_30,
       multiplexer_16_out, register_3_q, register_4_q;
  wire [7:0] iftoex_1_output_bus_3, multiplexer_8_out, multiplexer_11_out, multiplexer_12_out,
       multiplexer_13_out, multiplexer_14_out, multiplexer_17_out, multiplexer_18_out, RAM_1_dout,
       register0_1_out0, register0_1_out1;
  wire [15:0] add1_1_output_bus_1, addorsub_1_out_4, alu_1_output_bus_2, iftoex_1_out_20,
       iftoex_1_output_bus_2, multiplexer_1_out, multiplexer_2_out, multiplexer_3_out, multiplexer_4_out,
       multiplexer_5_out, multiplexer_6_out, multiplexer_7_out, register_1_q, register_2_q, ROM_2_data;
  wire [16:0] multiplexer_10_out, rom_2_data_2, rom_3_data;
  wire [20:0] rom_1_data;

  D_Flip_Flop d_ff_1 (.D(\中断信号 ), .clk(clock_1_out), .Q(d_ff_1_q), .reset(in_1));  // open: Qn, preset
  Clock clock_1 (.out(clock_1_out));
  D_Flip_Flop d_ff_2 (.D(d_ff_1_q), .clk(clock_2_out), .Q(d_ff_2_q), .reset(in_1));  // open: Qn, preset
  Clock clock_2 (.out(clock_2_out));
  Clock clock_3 (.out(clock_3_out));
  J_K_Flip_Flop j_k_ff_1 (
    .J(d_ff_2_q), .K(rom_1_data[17]), .clk(CLK), .Q(j_k_ff_1_q), .Qn(j_k_ff_1_qn), .reset(in_1));  // open: preset
  Multiplexer #(.width(16)) multiplexer_1 (
    .in0(multiplexer_4_out), .in1(in_3), .out(multiplexer_1_out), .sel(and_3_out));
  J_K_Flip_Flop j_k_ff_2 (
    .J(d_ff_2_q), .K(rom_1_data[18]), .clk(clock_3_out), .Q(j_k_ff_2_q), .preset(in_1));  // open: Qn, reset
  Register #(.width(16)) register_1 (.D(multiplexer_4_out), .en(and_2_out), .clk(CLK), .Q(register_1_q), .clr(in_1));
  and and_1 (CLK, j_k_ff_2_q, clock_4_out);
  Clock clock_4 (.out(clock_4_out));
  D_Flip_Flop d_ff_3 (.D(or_1_out), .clk(CLK), .Qn(d_ff_3_qn), .reset(in_1));  // open: Q, preset
  or or_1 (or_1_out, d_ff_2_q, j_k_ff_1_q);
  and and_2 (and_2_out, j_k_ff_1_qn, d_ff_2_q);
  Multiplexer #(.width(16)) multiplexer_2 (
    .in0(multiplexer_1_out), .in1(register_1_q), .out(multiplexer_2_out), .sel(rom_1_data[17]));
  Multiplexer #(.width(16)) multiplexer_3 (
    .in0(multiplexer_5_out), .in1(iftoex_1_output_bus_2), .out(multiplexer_3_out), .sel(iftoex_1_out_31));
  Multiplexer #(.width(16)) multiplexer_4 (
    .in0(multiplexer_3_out), .in1(addorsub_1_out_4), .out(multiplexer_4_out), .sel(iftoex_1_out_34));
  Register #(.width(16)) register_2 (.D(multiplexer_2_out), .en(1'b1), .clk(CLK), .Q(register_2_q), .clr(in_1));
  and and_3 (and_3_out, or_1_out, d_ff_3_qn);
  Multiplexer #(.select(2), .width(16)) multiplexer_5 (
    .in0(add1_1_output_bus_1), .in1(multiplexer_7_out), .in2(addorsub_1_out_4), .in3(add1_1_output_bus_1),
    .out(multiplexer_5_out), .sel(iftoex_1_out_21));
  and and_4 (and_4_out, iftoex_1_out_31, ~iftoex_1_out_34);  // AND_Gate
  Multiplexer #(.width(16)) multiplexer_6 (
    .in0(multiplexer_3_out), .in1(multiplexer_5_out), .out(multiplexer_6_out), .sel(and_4_out));
  Multiplexer #(.width(16)) multiplexer_7 (
    .in0(add1_1_output_bus_1), .in1(addorsub_1_out_4), .out(multiplexer_7_out), .sel(multiplexer_15_out));
  ADD1 add1_1 (.Input_bus_1(register_2_q), .Output_bus_1(add1_1_output_bus_1));
  ADDorSUB addorsub_1 (
    .in_2({{8{1'b0}}, iftoex_1_output_bus_2[7:0]}), .in_3(iftoex_1_out_20), .in_1(iftoex_1_out_36),
    .out_4(addorsub_1_out_4));
  ROM #(.addrWidth(16), .dataWidth(16)) ROM_2 (.addr(register_2_q), .data(ROM_2_data));
  ROM #(.addrWidth(4), .dataWidth(21)) rom_1 (.addr(ROM_2_data[15:12]), .data(rom_1_data));
  ROM #(.addrWidth(4), .dataWidth(17)) rom_2_dup2 (.addr(ROM_2_data[3:0]), .data(rom_2_data_2));
  ROM #(.addrWidth(4), .dataWidth(17)) rom_3 (.addr(ROM_2_data[3:0]), .data(rom_3_data));
  or or_2 (or_2_out, iftoex_1_out_31, iftoex_1_out_34);
  Multiplexer #(.width(8)) multiplexer_8 (
    .in0(multiplexer_18_out), .in1(multiplexer_6_out[7:0]), .out(multiplexer_8_out), .sel(or_2_out));
  Multiplexer #(.width(2)) multiplexer_9 (
    .in0(ROM_2_data[7:6]), .in1(ROM_2_data[9:8]), .out(multiplexer_9_out), .sel(multiplexer_10_out[12]));
  assign xor_1_out = ROM_2_data[11:10] ^ iftoex_1_output_bus_4;  // XOR_Gate xor_1, 2 bits wide
  nor nor_1 (nor_1_out, xor_1_out[1], not_1_out, xor_1_out[0]);
  nor nor_2 (nor_2_out, xor_3_out[1], not_1_out, xor_3_out[0]);
  assign xor_2_out = ROM_2_data[11:10] ^ register0_1_out_12;  // XOR_Gate xor_2, 2 bits wide
  nor nor_3 (nor_3_out, xor_2_out[1], not_2_out, xor_2_out[0]);
  nor nor_4 (nor_4_out, xor_4_out[1], not_2_out, xor_4_out[0]);
  Register0 register0_1 (
    .WE(iftoex_1_out_35), .in_9(iftoex_1_out_27), .WA(iftoex_1_output_bus_4), .RS(in_1), .C(CLK),
    .WIN(multiplexer_8_out), .in_2(multiplexer_6_out[15:8]), .RA1(ROM_2_data[9:8]), .RA0(ROM_2_data[11:10]),
    .out_12(register0_1_out_12), .OUT0(register0_1_out0), .OUT1(register0_1_out1));
  assign xor_3_out = ROM_2_data[9:8] ^ iftoex_1_output_bus_4;  // XOR_Gate xor_3, 2 bits wide
  not not_1 (not_1_out, iftoex_1_out_35);
  assign xor_4_out = ROM_2_data[9:8] ^ register0_1_out_12;  // XOR_Gate xor_4, 2 bits wide
  not not_2 (not_2_out, iftoex_1_out_27);
  Multiplexer #(.select(2), .width(17)) multiplexer_10 (
    .in0(rom_1_data[16:0]), .in1(rom_2_data_2), .in2(rom_3_data), .in3(rom_1_data[16:0]),
    .out(multiplexer_10_out), .sel(rom_1_data[20:19]));
  Multiplexer #(.width(8)) multiplexer_11 (
    .in0(register0_1_out0), .in1(multiplexer_18_out), .out(multiplexer_11_out), .sel(or_3_out));
  Multiplexer #(.width(8)) multiplexer_12 (
    .in0({multiplexer_9_out, ROM_2_data[5:0]}), .in1(ROM_2_data[11:4]), .out(multiplexer_12_out),
    .sel(multiplexer_10_out[16]));
  or or_3 (or_3_out, nor_1_out, nor_3_out);
  or or_4 (or_4_out, nor_2_out, nor_4_out);
  Multiplexer #(.width(8)) multiplexer_13 (
    .in0(register0_1_out1), .in1(multiplexer_18_out), .out(multiplexer_13_out), .sel(or_4_out));
  Multiplexer #(.width(8)) multiplexer_14 (
    .in0(multiplexer_13_out), .in1(multiplexer_12_out), .out(multiplexer_14_out), .sel(multiplexer_10_out[10]));
  IFtoEX iftoex_1 (
    .in_2(register_2_q), .in_7(j_k_ff_1_qn), .in_12(multiplexer_10_out[1]), .in_16(multiplexer_10_out[2]),
    .in_19(multiplexer_10_out[0]), .in_4(multiplexer_10_out[4:3]), .in_9(multiplexer_10_out[6:5]),
    .in_13(multiplexer_10_out[9:7]), .in_18(multiplexer_10_out[11]), .in_10(multiplexer_10_out[13]),
    .in_14(multiplexer_10_out[14]), .in_5(multiplexer_10_out[12]), .in_17(multiplexer_10_out[15]),
    .Input_1(CLK), .Input_2(in_1), .Input_bus_1(multiplexer_11_out), .Input_bus_2(multiplexer_14_out),
    .Input_bus_3(multiplexer_13_out), .Input_bus_4(ROM_2_data[7:6]), .out_24(iftoex_1_out_24),
    .out_20(iftoex_1_out_20), .out_29(iftoex_1_out_29), .out_33(iftoex_1_out_33), .out_36(iftoex_1_out_36),
    .out_21(iftoex_1_out_21), .out_26(iftoex_1_out_26), .out_30(iftoex_1_out_30), .out_35(iftoex_1_out_35),
    .out_27(iftoex_1_out_27), .out_31(iftoex_1_out_31), .out_22(iftoex_1_out_22), .out_34(iftoex_1_out_34),
    .Output_bus_1(iftoex_1_output_bus_2[15:8]), .Output_bus_2(iftoex_1_output_bus_2[7:0]),
    .Output_bus_3(iftoex_1_output_bus_3), .Output_bus_4(iftoex_1_output_bus_4));
  ALU alu_1 (
    .Input_bus_3(iftoex_1_out_30), .Input_bus_1(iftoex_1_output_bus_2[15:8]),
    .Input_bus_2(iftoex_1_output_bus_2[7:0]), .Input_1(multiplexer_16_out[0]),
    .Output_bus_2(alu_1_output_bus_2[7:0]), .Output_bus_1(alu_1_output_bus_1));
  not not_3 (not_3_out, iftoex_1_out_24);
  Register #(.width(3)) register_3 (.D(demultiplexer_1_out0), .en(and_5_out), .clk(CLK), .Q(register_3_q), .clr(in_1));
  and and_5 (and_5_out, not_3_out, iftoex_1_out_22);
  Register #(.width(3)) register_4 (.D(demultiplexer_1_out1), .en(and_6_out), .clk(CLK), .Q(register_4_q), .clr(in_1));
  and and_6 (and_6_out, iftoex_1_out_24, iftoex_1_out_22);
  Demultiplexer #(.width(3)) demultiplexer_1 (
    .out0(demultiplexer_1_out0), .out1(demultiplexer_1_out1), .in(alu_1_output_bus_1), .sel(iftoex_1_out_24));
  and and_7 (and_7_out, alu_1_output_bus_2[7], alu_1_output_bus_2[6], alu_1_output_bus_2[5], alu_1_output_bus_2[4], alu_1_output_bus_2[3], alu_1_output_bus_2[2], alu_1_output_bus_2[1], alu_1_output_bus_2[0]);
  Multiplexer #(.select(2)) multiplexer_15 (
    .in0(multiplexer_16_out[0]), .in1(multiplexer_16_out[1]), .in2(multiplexer_16_out[2]), .in3(1'b0),
    .out(multiplexer_15_out), .sel(iftoex_1_out_26));
  Multiplexer #(.width(3)) multiplexer_16 (
    .in0(register_3_q), .in1(register_4_q), .out(multiplexer_16_out), .sel(iftoex_1_out_24));
  RAM #(.addrWidth(16), .asyncread("true"), .clearpin("true")) RAM_1 (
    .addr(alu_1_output_bus_2), .we(iftoex_1_out_33), .oe(1'b1), .clk(CLK), .din(iftoex_1_output_bus_3),
    .dout(RAM_1_dout), .clr(in_1));
  Register register_5 (
    .D(alu_1_output_bus_2[7:0]), .en(and_8_out), .clk(CLK), .Q(alu_1_output_bus_2[15:8]), .clr(in_1));
  and and_8 (and_8_out, iftoex_1_out_33, and_7_out);
  not not_4 (not_4_out, iftoex_1_out_29);
  Multiplexer #(.width(8)) multiplexer_17 (
    .in0(RAM_1_dout), .in1(alu_1_output_bus_2[15:8]), .out(multiplexer_17_out), .sel(and_7_out));
  Multiplexer #(.width(8)) multiplexer_18 (
    .in0(multiplexer_17_out), .in1(alu_1_output_bus_2[7:0]), .out(multiplexer_18_out), .sel(not_4_out));

  // Other names for the same wires on the sheet: RST = in_1

  // Notes on the sheet:
  //   打拍
  //   NEXT
  //   中断向量
  //   RETI
  //   中断
  //   HLT
  //   中断状态
  //   搞SYSCALL！
  //   HLT
  //   中断状态
  //   影子PC
  //   跳转
  //   中断返回
  //   PC
  //   contents of ROM_2 (hex, n*v repeats v):
  //   1001 b482 c023 8400 ffff
  //   contents of rom_1 (hex, n*v repeats v):
  //   0 1c00 1d00 1e00 1e80 1f00 1500 c02 404 a800 a801 80000 100000 10404 20000 40000
  //   contents of rom_2 (hex, n*v repeats v):
  //   1800 1880 1900 1980 1a00 1a80 1b00 1b80 1100
  //   contents of rom_3 (hex, n*v repeats v):
  //   10410 10411 10408 10409 10428 10429 10448 10449 10 11 6800
  //   加更新标志位选择！
  //   加IO！
endmodule

module ALU (
  input  Input_1,
  input  [7:0] Input_bus_1,
  input  [7:0] Input_bus_2,
  input  [2:0] Input_bus_3,
  output [2:0] Output_bus_1,
  output [7:0] Output_bus_2
);

  wire adder_1_cout, decoder_1_out0, decoder_1_out1, decoder_1_out2, decoder_1_out3, decoder_1_out4,
       decoder_1_out5, decoder_1_out6, decoder_1_out7, multiplexer_1_out, or_1_out, or_4_out;
  wire [7:0] adder_1_out, and_1_out, or_3_out, xor_1_out, xor_2_out;
  wire [7:7] or_2_out;

  Decoder #(.enable("false"), .select(3)) decoder_1 (
    .out0(decoder_1_out0), .out1(decoder_1_out1), .out2(decoder_1_out2), .out3(decoder_1_out3),
    .out4(decoder_1_out4), .out5(decoder_1_out5), .out6(decoder_1_out6), .out7(decoder_1_out7),
    .sel(Input_bus_3));
  or or_1 (or_1_out, decoder_1_out1, decoder_1_out3);
  or or_2 (or_2_out[7], decoder_1_out2, decoder_1_out3);
  assign xor_1_out = {8{or_2_out[7]}} ^ Input_bus_2;  // XOR_Gate xor_1, 8 bits wide
  assign and_1_out = Input_bus_1 & Input_bus_2;  // AND_Gate and_1, 8 bits wide
  assign or_3_out = Input_bus_1 | Input_bus_2;  // OR_Gate or_3, 8 bits wide
  assign xor_2_out = Input_bus_1 ^ Input_bus_2;  // XOR_Gate xor_2, 8 bits wide
  or or_4 (or_4_out, decoder_1_out0, decoder_1_out1, decoder_1_out2, decoder_1_out3);
  Multiplexer multiplexer_1 (.in0(or_2_out[7]), .in1(Input_1), .out(multiplexer_1_out), .sel(or_1_out));
  Adder adder_1 (.a(Input_bus_1), .b(xor_1_out), .out(adder_1_out), .cin(multiplexer_1_out), .cout(adder_1_cout));
  nor nor_1 (Output_bus_1[1], xor_2_out[7], xor_2_out[6], xor_2_out[5], xor_2_out[4], xor_2_out[3], xor_2_out[2], xor_2_out[1], xor_2_out[0]);
  not not_1 (Output_bus_1[0], adder_1_cout);
  assign Output_bus_2 = decoder_1_out6 ? xor_2_out : 8'bz;  // Controlled_Buffer controlled_buffer_1
  assign Output_bus_2 = decoder_1_out7 ? {1'b0, Input_bus_1[7:1]} : 8'bz;  // Controlled_Buffer controlled_buffer_2
  assign Output_bus_2 = or_4_out ? adder_1_out : 8'bz;  // Controlled_Buffer controlled_buffer_3
  assign Output_bus_2 = decoder_1_out4 ? and_1_out : 8'bz;  // Controlled_Buffer controlled_buffer_4
  assign Output_bus_2 = decoder_1_out5 ? or_3_out : 8'bz;  // Controlled_Buffer controlled_buffer_5

  assign Output_bus_1[2] = Input_bus_1[0];

  // Notes on the sheet:
  //   A
  //   B
endmodule

module Register0 (
  input  [7:0] WIN,
  input  [7:0] in_2,
  input  RS,
  input  [1:0] RA0,
  input  C,
  input  WE,
  input  [1:0] WA,
  input  [1:0] RA1,
  input  in_9,
  output [7:0] OUT0,
  output [7:0] OUT1,
  output [1:0] out_12
);

  wire decoder_1_out0, decoder_1_out1, decoder_1_out2, decoder_1_out3, decoder_2_out0, decoder_2_out1,
       decoder_2_out2, decoder_2_out3, or_1_out, or_2_out, or_3_out, or_4_out;
  wire [1:0] adder_2_out, multiplexer_3_out;
  wire [7:0] controlled_buffer_1_out, controlled_buffer_3_out, controlled_buffer_5_out,
       controlled_buffer_7_out, register_1_q, register_2_q, register_3_q, register_4_q;

  Decoder #(.select(2)) decoder_1 (
    .out0(decoder_1_out0), .out1(decoder_1_out1), .out2(decoder_1_out2), .out3(decoder_1_out3), .sel(WA),
    .en(WE));
  Decoder #(.select(2)) decoder_2 (
    .out0(decoder_2_out0), .out1(decoder_2_out1), .out2(decoder_2_out2), .out3(decoder_2_out3), .sel(out_12),
    .en(in_9));
  Adder #(.width(2)) adder_1 (.a(WA), .b(2'b01), .out(out_12));  // open: cin, cout
  assign controlled_buffer_1_out = decoder_1_out0 ? WIN : 8'bz;  // Controlled_Buffer controlled_buffer_1
  assign controlled_buffer_1_out = decoder_2_out0 ? in_2 : 8'bz;  // Controlled_Buffer controlled_buffer_2
  or or_1 (or_1_out, decoder_1_out0, decoder_2_out0);
  assign controlled_buffer_3_out = decoder_1_out1 ? WIN : 8'bz;  // Controlled_Buffer controlled_buffer_3
  assign controlled_buffer_3_out = decoder_2_out1 ? in_2 : 8'bz;  // Controlled_Buffer controlled_buffer_4
  or or_2 (or_2_out, decoder_1_out1, decoder_2_out1);
  assign controlled_buffer_5_out = decoder_1_out2 ? WIN : 8'bz;  // Controlled_Buffer controlled_buffer_5
  assign controlled_buffer_5_out = decoder_2_out2 ? in_2 : 8'bz;  // Controlled_Buffer controlled_buffer_6
  or or_3 (or_3_out, decoder_1_out2, decoder_2_out2);
  assign controlled_buffer_7_out = decoder_1_out3 ? WIN : 8'bz;  // Controlled_Buffer controlled_buffer_7
  assign controlled_buffer_7_out = decoder_2_out3 ? in_2 : 8'bz;  // Controlled_Buffer controlled_buffer_8
  or or_4 (or_4_out, decoder_1_out3, decoder_2_out3);
  Register register_1 (.D(controlled_buffer_1_out), .en(or_1_out), .clk(C), .Q(register_1_q), .clr(RS));
  Register register_2 (.D(controlled_buffer_3_out), .en(or_2_out), .clk(C), .Q(register_2_q), .clr(RS));
  Register register_3 (.D(controlled_buffer_5_out), .en(or_3_out), .clk(C), .Q(register_3_q), .clr(RS));
  Register register_4 (.D(controlled_buffer_7_out), .en(or_4_out), .clk(C), .Q(register_4_q), .clr(RS));
  Adder #(.width(2)) adder_2 (.a(RA0), .b(2'b01), .out(adder_2_out));  // open: cin, cout
  Multiplexer #(.select(2), .width(8)) multiplexer_1 (
    .in0(register_1_q), .in1(register_2_q), .in2(register_3_q), .in3(register_4_q), .out(OUT0), .sel(RA0));
  Multiplexer #(.select(2), .width(8)) multiplexer_2 (
    .in0(register_1_q), .in1(register_2_q), .in2(register_3_q), .in3(register_4_q), .out(OUT1),
    .sel(multiplexer_3_out));
  Multiplexer #(.width(2)) multiplexer_3 (.in0(RA1), .in1(adder_2_out), .out(multiplexer_3_out), .sel(in_9));

  // Other names for the same wires on the sheet: CLK = C
endmodule

module ADD1 (
  input  [15:0] Input_bus_1,
  output [15:0] Output_bus_1
);

  Adder #(.width(16)) adder_1 (.a(Input_bus_1), .b(16'h1), .out(Output_bus_1));  // open: cin, cout
endmodule

module IFtoEX (
  input  Input_1,
  input  [15:0] in_2,
  input  Input_2,
  input  [1:0] in_4,
  input  in_5,
  input  [7:0] Input_bus_1,
  input  in_7,
  input  [7:0] Input_bus_2,
  input  [1:0] in_9,
  input  in_10,
  input  [7:0] Input_bus_3,
  input  in_12,
  input  [2:0] in_13,
  input  in_14,
  input  [1:0] Input_bus_4,
  input  in_16,
  input  in_17,
  input  in_18,
  input  in_19,
  output [15:0] out_20,
  output [1:0] out_21,
  output out_22,
  output [7:0] Output_bus_1,
  output out_24,
  output [7:0] Output_bus_2,
  output [1:0] out_26,
  output out_27,
  output [7:0] Output_bus_3,
  output out_29,
  output [2:0] out_30,
  output out_31,
  output [1:0] Output_bus_4,
  output out_33,
  output out_34,
  output out_35,
  output out_36
);

  Register register_1 (.D(Input_bus_1), .en(1'b1), .clk(Input_1), .Q(Output_bus_1), .clr(Input_2));
  Register register_2 (.D(Input_bus_2), .en(1'b1), .clk(Input_1), .Q(Output_bus_2), .clr(Input_2));
  Register register_3 (.D(Input_bus_3), .en(1'b1), .clk(Input_1), .Q(Output_bus_3), .clr(Input_2));
  Register #(.width(2)) register_4 (.D(Input_bus_4), .en(1'b1), .clk(Input_1), .Q(Output_bus_4), .clr(Input_2));
  Register #(.width(16)) register_5 (.D(in_2), .en(1'b1), .clk(Input_1), .Q(out_20), .clr(Input_2));
  Register #(.width(1)) register_6 (.D(in_7), .en(1'b1), .clk(Input_1), .Q(out_24), .clr(Input_2));
  Register #(.width(1)) register_7 (.D(in_12), .en(1'b1), .clk(Input_1), .Q(out_29), .clr(Input_2));
  Register #(.width(1)) register_8 (.D(in_16), .en(1'b1), .clk(Input_1), .Q(out_33), .clr(Input_2));
  Register #(.width(1)) register_9 (.D(in_19), .en(1'b1), .clk(Input_1), .Q(out_36), .clr(Input_2));
  Register #(.width(2)) register_10 (.D(in_4), .en(1'b1), .clk(Input_1), .Q(out_21), .clr(Input_2));
  Register #(.width(2)) register_11 (.D(in_9), .en(1'b1), .clk(Input_1), .Q(out_26), .clr(Input_2));
  Register #(.width(3)) register_12 (.D(in_13), .en(1'b1), .clk(Input_1), .Q(out_30), .clr(Input_2));
  Register #(.width(1)) register_13 (.D(in_18), .en(1'b1), .clk(Input_1), .Q(out_35), .clr(Input_2));
  Register #(.width(1)) register_14 (.D(in_5), .en(1'b1), .clk(Input_1), .Q(out_22), .clr(Input_2));
  Register #(.width(1)) register_15 (.D(in_10), .en(1'b1), .clk(Input_1), .Q(out_27), .clr(Input_2));
  Register #(.width(1)) register_16 (.D(in_14), .en(1'b1), .clk(Input_1), .Q(out_31), .clr(Input_2));
  Register #(.width(1)) register_17 (.D(in_17), .en(1'b1), .clk(Input_1), .Q(out_34), .clr(Input_2));

  // Other names for the same wires on the sheet: CLK = Input_1; RS = Input_2
endmodule

module ADDorSUB (
  input  in_1,
  input  [15:0] in_2,
  input  [15:0] in_3,
  output [15:0] out_4
);

  wire [15:0] xor_1_out;

  assign xor_1_out = in_3 ^ {16{in_1}};  // XOR_Gate xor_1, 16 bits wide
  Adder #(.width(16)) adder_1 (.a(in_2), .b(xor_1_out), .out(out_4), .cin(in_1));  // open: cout
endmodule
